# Fritzing sketch inventor-01 (saved by Fritzing 0.9.3b)
breadboards: 1

parts:
  R1 = BBC MicroBit
  S1 = Pushbutton [package="[THT]"]
  S2 = Pushbutton [package="[THT]"]

nets:
  N1: R1.GND, S1.Pin_1, S1.Pin_2, S2.Pin_1, S2.Pin_2
  N2: R1.P18_+3v3, R1.P7
  N3: R1.P11_BUTTON_B, S2.Pin_3, S2.Pin_4
  N4: R1.P5_BUTTON_A, S1.Pin_3, S1.Pin_4

custom parts:
  BBC MicroBit: The BBC MICRO:BIT
