# Fritzing sketch inventor-02 (saved by Fritzing 0.9.3b)
breadboards: 1

parts:
  R1 = BBC MicroBit
  R2 = Photocell (LDR) [package=THT]
  R3 = Resistor [tolerance=±5% resistance=10k package="2512 [SMD]"]

nets:
  N1: R1.GND, R3.Pin_1
  N2: R1.3v3, R2.pin_0
  N3: R1.P0_ANALOG_IN, R2.pin_1, R3.Pin_0

custom parts:
  BBC MicroBit: The BBC MICRO:BIT
