# Fritzing sketch inventor-03 (saved by Fritzing 0.9.3b)
breadboards: 1

parts:
  R1 = BBC MicroBit
  LED1 = LED - 5mm [color="Red (633nm)" package="5 mm [THT]"]
  S1 = Pushbutton [package="[SMD]"]
  R1_2 = Resistor [tolerance=±5% resistance=47 package="2512 [SMD]"]
  U2 = POT [package=pot_alpha_rv16af-20]

nets:
  N1: R1.GND, LED1.cathode, S1.Pin_1, S1.Pin_2, U2.A
  N2: R1.3v3, U2.E
  N3: R1.P2_-_ANALOG_IN, R1_2.Pin_0
  N4: R1.P1_ANALOG_IN, U2.S
  N5: R1.P7, R1.P6, R1.P5_BUTTON_A
  N6: R1.P0_ANALOG_IN, S1.Pin_3, S1.Pin_4
  N7: LED1.anode, R1_2.Pin_1

custom parts:
  BBC MicroBit: The BBC MICRO:BIT
